// Logisim project 3bit-counter-1D-2JK.circ as structural Verilog: 1 circuit, main circuit main
module main (
  input  CLK,
  output Z0,
  output Z1,
  output Z2
);

  wire and_1_out, d_ff_1_qn;

  D_Flip_Flop d_ff_1 (.clk(CLK), .D(d_ff_1_qn), .Q(Z0), .Qn(d_ff_1_qn));  // open: preset, en, reset
  J_K_Flip_Flop j_k_ff_1 (.J(Z0), .clk(CLK), .K(Z0), .Q(Z1));  // open: Qn, preset, en, reset
  and and_1 (and_1_out, Z0, Z1);
  J_K_Flip_Flop j_k_ff_2 (.J(and_1_out), .clk(CLK), .K(and_1_out), .Q(Z2));  // open: Qn, preset, en, reset

  // Notes on the sheet:
  //   Z0 is the least significant bit
endmodule
