// Logisim project lab11.circ as structural Verilog: 1 circuit, main circuit main
module main (
  input  X,
  output Q2,
  output Q1,
  output Q0
);

  wire and_1_out, and_2_out, and_3_out, and_4_out, and_5_out, and_6_out, and_7_out, and_8_out, and_9_out,
       and_10_out, and_11_out, and_12_out, and_13_out, clock_1_out, d_ff_1_qn, j_k_ff_1_qn, not_1_out,
       or_1_out, or_2_out, or_3_out, t_ff_1_qn;

  Clock clock_1 (.out(clock_1_out));
  not not_1 (not_1_out, X);
  and and_1 (and_1_out, not_1_out, Q1);
  and and_2 (and_2_out, not_1_out, Q0);
  and and_3 (and_3_out, Q2, Q1, d_ff_1_qn);
  and and_4 (and_4_out, j_k_ff_1_qn, Q0);
  and and_5 (and_5_out, X, t_ff_1_qn);
  or or_1 (or_1_out, and_1_out, and_2_out, and_3_out, and_4_out, and_5_out);
  J_K_Flip_Flop j_k_ff_1 (
    .J(or_1_out), .clk(clock_1_out), .K(or_1_out), .Q(Q2), .Qn(j_k_ff_1_qn));  // open: preset, en, reset
  and and_6 (and_6_out, Q2, t_ff_1_qn);
  and and_7 (and_7_out, not_1_out, Q2, d_ff_1_qn);
  and and_8 (and_8_out, X, t_ff_1_qn);
  and and_9 (and_9_out, not_1_out, j_k_ff_1_qn, Q1, Q0);
  D_Flip_Flop d_ff_1 (.clk(clock_1_out), .D(or_2_out), .Q(Q0), .Qn(d_ff_1_qn));  // open: preset, en, reset
  or or_2 (or_2_out, and_6_out, and_7_out, and_8_out, and_9_out);
  and and_10 (and_10_out, not_1_out, t_ff_1_qn, d_ff_1_qn);
  and and_11 (and_11_out, not_1_out, Q1, Q0);
  and and_12 (and_12_out, X, Q2, Q0);
  and and_13 (and_13_out, X, j_k_ff_1_qn, d_ff_1_qn);
  or or_3 (or_3_out, and_10_out, and_11_out, and_12_out, and_13_out);
  T_Flip_Flop t_ff_1 (.clk(clock_1_out), .T(or_3_out), .Q(Q1), .Qn(t_ff_1_qn));  // open: preset, reset, en

  // Notes on the sheet:
  //   Q2
  //   3 bit non-sequential counter
  //   Lab 11, 11/16/2011
  //   author(s): Jeremiah Mahler, Marvanee Johnson
  //   Q0
  //   Q1
endmodule
