// Logisim project Lab2-01.circ as structural Verilog: 1 circuit, main circuit main
module main (
  input  A,
  input  B,
  input  C,
  output out_4
);

  wire and_1_out, and_2_out, not_1_out;

  and and_1 (and_1_out, A, B);
  not not_1 (not_1_out, C);
  and and_2 (and_2_out, A, B, C);
  or or_1 (out_4, and_1_out, not_1_out, and_2_out);

  // Notes on the sheet:
  //   A B
  //   C'
  //   A B C
  //   A B + C' + A B C
endmodule
