// Logisim project Lab2-02.circ as structural Verilog: 1 circuit, main circuit main
module main (
  input  a,
  input  b,
  input  c,
  output out_4
);

  wire and_1_out, not_1_out;

  and and_1 (and_1_out, a, b);
  not not_1 (not_1_out, c);
  or or_1 (out_4, not_1_out, and_1_out);

  // Notes on the sheet:
  //   ab
  //   c'
  //   ab+c'
endmodule
