// Logisim project Lab3-circuit.circ as structural Verilog: 1 circuit, main circuit main
module main (
  input  a,
  input  b,
  input  c,
  output out_4
);

  wire and_1_out, and_2_out, and_3_out, and_4_out, not_1_out, not_2_out, not_3_out, or_1_out;

  not not_1 (not_1_out, a);
  not not_2 (not_2_out, b);
  not not_3 (not_3_out, c);
  and and_1 (and_1_out, a, c);
  and and_2 (and_2_out, not_1_out, b);
  and and_3 (and_3_out, not_2_out, not_3_out);
  and and_4 (and_4_out, a, and_3_out);
  or or_1 (or_1_out, and_1_out, and_2_out);
  or or_2 (out_4, or_1_out, and_4_out);

  // Notes on the sheet:
  //   a c
  //   a' b
  //   a b' c'
  //   a c + a' b + a b' c'
endmodule
