// Logisim project JKjoint-01.circ as structural Verilog: 1 circuit, main circuit main
module main (
  input  w,
  input  x,
  input  y,
  input  z,
  output J,
  output K
);

  wire and_1_out, and_2_out, and_3_out, and_4_out, and_5_out, and_6_out, and_7_out, not_1_out, not_2_out,
       not_3_out, not_4_out, or_1_out, or_2_out;

  not not_1 (not_1_out, w);
  not not_2 (not_2_out, x);
  not not_3 (not_3_out, y);
  not not_4 (not_4_out, z);
  and and_1 (and_1_out, not_1_out, not_2_out);
  and and_2 (and_2_out, w, x);
  and and_3 (and_3_out, w, z);
  and and_4 (and_4_out, not_1_out, not_2_out);
  and and_5 (and_5_out, and_1_out, z);
  and and_6 (and_6_out, and_2_out, not_4_out);
  and and_7 (and_7_out, and_4_out, not_3_out);
  or or_1 (or_1_out, and_5_out, and_6_out);
  or or_2 (or_2_out, and_5_out, and_6_out);
  or or_3 (J, or_1_out, and_3_out);
  or or_4 (K, or_2_out, and_7_out);

  // Notes on the sheet:
  //   w'x'z
  //   wxz'
  //   wz
  //   w'x'y'
endmodule
