// Logisim project Jminsop-01.circ as structural Verilog: 1 circuit, main circuit main
module main (
  input  w,
  input  x,
  input  y,
  input  z,
  output out_5
);

  wire and_1_out, and_2_out, not_1_out;

  not not_1 (not_1_out, x);
  and and_1 (and_1_out, w, x);
  and and_2 (and_2_out, not_1_out, z);
  or or_1 (out_5, and_1_out, and_2_out);
endmodule
