// Logisim project lab8-marv_comb-01.circ as structural Verilog: 2 circuits, main circuit main
module main (
  input  [2:0] a_1_b,
  input  [2:0] c_1_d,
  output out_3
);

  wire decoder_1_out0, decoder_1_out1, decoder_1_out2, decoder_1_out3, decoder_1_out4, decoder_1_out5,
       decoder_1_out6, decoder_1_out7, not_3_out, not_4_out, not_7_out, not_8_out;

  Decoder #(.select(3), .enable("false")) decoder_1 (
    .out0(decoder_1_out0), .out1(decoder_1_out1), .out2(decoder_1_out2), .out3(decoder_1_out3),
    .out4(decoder_1_out4), .out5(decoder_1_out5), .out6(decoder_1_out6), .out7(decoder_1_out7), .sel(a_1_b));
  // NOT_Gate not_1 has open pins: in=decoder_1_out0, out=open
  // NOT_Gate not_2 has open pins: in=decoder_1_out1, out=open
  not not_3 (not_3_out, decoder_1_out2);
  not not_4 (not_4_out, decoder_1_out3);
  // NOT_Gate not_5 has open pins: in=decoder_1_out4, out=open
  // NOT_Gate not_6 has open pins: in=decoder_1_out5, out=open
  not not_7 (not_7_out, decoder_1_out6);
  not not_8 (not_8_out, decoder_1_out7);
  Multiplexer #(.select(3), .enable("false")) multiplexer_1 (
    .in0(1'b1), .in1(1'b1), .in2(not_7_out), .in3(not_4_out), .in4(1'b1), .in5(1'b1), .in6(not_3_out),
    .in7(not_8_out), .out(out_3), .sel(c_1_d));
endmodule

module test1 (
  input  a,
  input  b,
  input  c,
  input  d,
  output z
);

  wire and_1_out, and_2_out, not_1_out, not_2_out, not_3_out, not_4_out, not_5_out, not_6_out, not_7_out,
       not_8_out, or_1_out, or_2_out, or_3_out, or_4_out, or_5_out, or_6_out, or_7_out, or_8_out, or_9_out,
       or_10_out, or_11_out, or_12_out;

  or or_1 (or_1_out, a, b);
  or or_2 (or_2_out, c, d);
  or or_3 (or_3_out, a, not_1_out);
  not not_1 (not_1_out, b);
  not not_2 (not_2_out, c);
  or or_4 (or_4_out, not_2_out, not_3_out);
  not not_3 (not_3_out, d);
  not not_4 (not_4_out, a);
  or or_5 (or_5_out, not_4_out, b);
  not not_5 (not_5_out, c);
  or or_6 (or_6_out, not_5_out, d);
  not not_6 (not_6_out, a);
  or or_7 (or_7_out, not_6_out, not_7_out);
  not not_7 (not_7_out, b);
  or or_8 (or_8_out, c, not_8_out);
  not not_8 (not_8_out, d);
  or or_9 (or_9_out, or_1_out, or_2_out);
  or or_10 (or_10_out, or_3_out, or_4_out);
  or or_11 (or_11_out, or_5_out, or_6_out);
  or or_12 (or_12_out, or_7_out, or_8_out);
  and and_1 (and_1_out, or_9_out, or_10_out);
  and and_2 (and_2_out, or_11_out, or_12_out);
  and and_3 (z, and_1_out, and_2_out);
endmodule
